// Logisim project mips_processor.circ as structural Verilog
module IF_ID (
  input  CLEAR,
  input  [31:0] INSTRUCTION,
  input  [31:0] PC,
  input  ENABLE,
  input  CLK,
  output [5:0] OPCODE,
  output [4:0] RS,
  output [4:0] RT,
  output [4:0] RD,
  output [4:0] SHAMT,
  output [5:0] FUNCT,
  output [15:0] IMMEDIATE,
  output [25:0] ADDRESS,
  output [31:0] PC_2
);

  wire not_1_out;

  Register #(.width(32)) u_instruction (
    .D(INSTRUCTION), .en(ENABLE), .Q({OPCODE, ADDRESS}), .clk(not_1_out), .clr(CLEAR));
  Register #(.width(32)) program_counter (.D(PC), .en(ENABLE), .Q(PC_2), .clk(not_1_out), .clr(CLEAR));
  not not_1 (not_1_out, CLK);

  assign FUNCT = ADDRESS[5:0];
  assign IMMEDIATE = ADDRESS[15:0];
  assign RD = ADDRESS[15:11];
  assign RS = ADDRESS[25:21];
  assign RT = ADDRESS[20:16];
  assign SHAMT = ADDRESS[10:6];
endmodule

module ID_EX (
  input  CLEAR,
  input  [31:0] PC,
  input  RegWrite,
  input  MemToReg,
  input  MemWrite,
  input  MemRead,
  input  Branch,
  input  [1:0] AluOp,
  input  RegDst,
  input  AluSrc,
  input  [31:0] ReadData1,
  input  [31:0] ReadData2,
  input  [31:0] Immediate,
  input  [4:0] RT,
  input  [4:0] RD,
  input  ENABLE,
  input  CLK,
  output [31:0] PC_2,
  output RegWrite_2,
  output MemToReg_2,
  output MemWrite_2,
  output MemRead_2,
  output Branch_2,
  output [1:0] AluOp_2,
  output RegDst_2,
  output AluSrc_2,
  output [31:0] ReadData1_2,
  output [31:0] ReadData2_2,
  output [31:0] IMMEADIATE,
  output [4:0] RT_2,
  output [4:0] RD_2
);

  wire not_1_out;

  not not_1 (not_1_out, CLK);
  Register #(.width(32)) program_counter (.D(PC), .en(ENABLE), .Q(PC_2), .clk(not_1_out), .clr(CLEAR));
  Register #(.width(2)) wb (
    .D({RegWrite, MemToReg}), .en(ENABLE), .Q({RegWrite_2, MemToReg_2}), .clk(not_1_out), .clr(CLEAR));
  Register #(.width(3)) mem (
    .D({MemWrite, MemRead, Branch}), .en(ENABLE), .Q({MemWrite_2, MemRead_2, Branch_2}), .clk(not_1_out),
    .clr(CLEAR));
  Register #(.width(4)) ex (
    .D({AluOp, RegDst, AluSrc}), .en(ENABLE), .Q({AluOp_2, RegDst_2, AluSrc_2}), .clk(not_1_out), .clr(CLEAR));
  Register #(.width(32)) read_data1 (.D(ReadData1), .en(ENABLE), .Q(ReadData1_2), .clk(not_1_out), .clr(CLEAR));
  Register #(.width(32)) read_data2 (.D(ReadData2), .en(ENABLE), .Q(ReadData2_2), .clk(not_1_out), .clr(CLEAR));
  Register #(.width(32)) u_immediate (.D(Immediate), .en(ENABLE), .Q(IMMEADIATE), .clk(not_1_out), .clr(CLEAR));
  Register #(.width(5)) u_rt (.D(RT), .en(ENABLE), .Q(RT_2), .clk(not_1_out), .clr(CLEAR));
  Register #(.width(5)) u_rd (.D(RD), .en(ENABLE), .Q(RD_2), .clk(not_1_out), .clr(CLEAR));
endmodule

module EX_MEM (
  input  CLEAR,
  input  [31:0] Branch_Adress,
  input  [31:0] BranchAddress,
  input  [31:0] ADD_Result_Output,
  input  [31:0] ADD_Result,
  input  ALU_Zero,
  input  ALU_zero_Output,
  input  [31:0] ALU_Result,
  input  [31:0] ALU_Result_Output,
  input  [4:0] Write_reg,
  input  [4:0] Write_Reg_2,
  input  [1:0] WB,
  input  [1:0] WB_2,
  input  [2:0] MEM,
  input  [2:0] MEM_2,
  input  CLK
);

  wire [31:0] program_counter_q;

  Register #(.width(32)) program_counter (
    .D(BranchAddress), .Q(program_counter_q), .clk(CLK), .clr(CLEAR));  // open: en
  Register #(.width(5)) WriteReg (.D(Write_reg), .Q(Write_Reg_2), .clk(CLK), .clr(CLEAR));  // open: en
  Register #(.width(32)) u_ADD_Result (.D(ADD_Result), .Q(ADD_Result_Output), .clk(CLK), .clr(CLEAR));  // open: en
  Register #(.width(1)) u_ALU_Zero (.D(ALU_Zero), .Q(ALU_zero_Output), .clk(CLK), .clr(CLEAR));  // open: en
  Register #(.width(32)) u_ALU_Result (.D(ALU_Result), .Q(ALU_Result_Output), .clk(CLK), .clr(CLEAR));  // open: en
  Register #(.width(2)) u_WB (.D(WB), .Q(WB_2), .clk(CLK), .clr(CLEAR));  // open: en
  Register #(.width(3)) u_MEM (.D(MEM), .Q(MEM_2), .clk(CLK), .clr(CLEAR));  // open: en
endmodule

module MEM_WB (
  input  Clear,
  input  [4:0] Write_reg,
  input  [4:0] Write_reg_2,
  input  [31:0] Read_Data,
  input  [31:0] Read_Data_Output,
  input  [31:0] ALU_Result,
  input  [31:0] ALU_Result_Output,
  input  [1:0] WB,
  input  [1:0] WB_2,
  input  CLK
);

  Register #(.width(32)) Mem_Read (.D(ALU_Result), .Q(ALU_Result_Output), .clk(CLK), .clr(Clear));  // open: en
  Register #(.width(2)) Mem_Read_2 (.D(WB), .Q(WB_2), .clk(CLK), .clr(Clear));  // open: en
  Register #(.width(32)) u_Read_Data (.D(Read_Data), .Q(Read_Data_Output), .clk(CLK), .clr(Clear));  // open: en
  Register #(.width(5)) Read_Data_2 (.D(Write_reg_2), .Q(Write_reg), .clk(CLK), .clr(Clear));  // open: en
endmodule
